// Logisim project alu_stage17_builtin_mux_core6_zero.circ as structural Verilog: 1 circuit, main circuit alu_stage17_builtin_mux_core6_zero
module alu_stage17_builtin_mux_core6_zero (
  input  [31:0] A,
  input  [31:0] B,
  input  [3:0] ALUOp,
  input  [4:0] shamt,
  output Negative,
  output [31:0] Result,
  output Zero
);

  wire comparator_1_lt;
  wire [31:0] RADD, RAND, RDIV, RMUL, ROR, RSLL, RSLT, RSRA, RSRL, RSUB, RXOR;

  // Probe on A
  // Probe on B
  Subtractor #(.width(32)) subtractor_1 (.a(A), .b(B), .out(RSUB));  // open: bin, bout
  assign RAND = A & B;  // AND_Gate and_1, 32 bits wide
  assign ROR = A | B;  // OR_Gate or_1, 32 bits wide
  assign RXOR = A ^ B;  // XOR_Gate xor_1, 32 bits wide
  Multiplier #(.width(32)) multiplier_1 (.a(A), .b(B), .cout(RMUL));  // open: out, cin
  Divider #(.width(32)) divider_1 (.a(A), .b(B), .out(RDIV));  // open: upper, rem
  Comparator #(.width(32)) comparator_1 (.a(A), .b(B), .lt(comparator_1_lt));  // open: gt, eq
  Shifter #(.width(32)) shifter_1 (.in(B), .\dist (shamt), .out(RSLL));
  Shifter #(.width(32), .shift("lr")) shifter_2 (.in(B), .\dist (shamt), .out(RSRL));
  Shifter #(.width(32), .shift("ar")) shifter_3 (.in(B), .\dist (shamt), .out(RSRA));
  // Probe on ALUOp
  assign RSLT = {{31{1'b0}}, comparator_1_lt};  // Bit_Extender bit_extender_1
  Multiplexer #(.select(4), .width(32), .enable("false")) multiplexer_1 (
    .in0(RADD), .in1(RSUB), .in2(RMUL), .in3(RDIV), .in4(RAND), .in5(ROR), .in6(RXOR), .in7(RSLT),
    .in8(RSLL), .in9(RSRL), .in10(RSRA), .out({Negative, Result[30:0]}), .sel(ALUOp));  // open: in11, in12, in13, in14, in15
  // Probe on shamt
  Adder #(.width(32)) adder_1 (.a(A), .b(B), .out(RADD));  // open: cin, cout
  // Probe on {Negative, Result[30:0]}
  // Probe on Zero
  nor nor_1 (Zero, Result[0], Result[1], Result[2], Result[3], Result[4], Result[5], Result[6], Result[7], Result[8], Result[9], Result[10], Result[11], Result[12], Result[13], Result[14], Result[15], Result[17], Result[18], Result[19], Result[20], Result[21], Result[22], Result[23], Result[24], Result[25], Result[26], Result[27], Result[28], Result[29], Result[30], Negative);

  assign Result[31] = Negative;

  // Other names for the same wires on the sheet: A_BUS[31:0] = A; B_BUS[31:0] = B; SHAMT_BUS[4:0] = shamt
endmodule
