// Logisim project jednostka_sterujaca.circ as structural Verilog: 2 circuits, main circuit jednostka_sterujaca
module jednostka_sterujaca (
  input  [5:0] Opcode,
  input  [5:0] Funct,
  output [9:0] ControlWord,
  output RegDst,
  output ALUSrc,
  output MemtoReg,
  output RegWrite,
  output MemRead,
  output MemWrite,
  output Branch,
  output Jump,
  output ALUClass1,
  output ALUClass0,
  output [3:0] ALUOp
);

  ROM #(.addrWidth(6), .dataWidth(10)) rom_1 (
    .addr(Opcode),
    .data({ControlWord[9], ALUSrc, ControlWord[7:4], Branch, ControlWord[2], ALUClass1, ALUClass0}));  // open: sel
  // Probe on {ControlWord[9], ALUSrc, ControlWord[7:4], Branch, ControlWord[2], ALUClass1, ALUClass0}
  aluop_decode_local aluop_decode_local_1 (
    .Opcode(Opcode), .Funct(Funct), .ALUClass({ALUClass1, ALUClass0}), .ALUOp(ALUOp));

  assign {ControlWord[8], ControlWord[3], ControlWord[1:0]} = {ALUSrc, Branch, ALUClass1, ALUClass0};
  assign Jump = ControlWord[2];
  assign MemRead = ControlWord[5];
  assign MemtoReg = ControlWord[7];
  assign MemWrite = ControlWord[4];
  assign RegDst = ControlWord[9];
  assign RegWrite = ControlWord[6];

  // Other names for the same wires on the sheet: ALUC0_CTL = ALUClass0; ALUC1_CTL = ALUClass1; FUNCT_CTL[5:0] = Funct;
  //   OPCODE_CTL[5:0] = Opcode

  // Notes on the sheet:
  //   contents of rom_1 (hex, n*v repeats v):
  //   242 0 4 0 4*9 140 0 143 0 143 143 143 20*0 1e0 7*0 110
endmodule

module aluop_decode_local (
  input  [5:0] Opcode,
  input  [5:0] Funct,
  input  [1:0] ALUClass,
  output [3:0] ALUOp
);

  wire [3:0] rom_1_data, rom_2_data;

  // Probe on rom_1_data
  ROM #(.addrWidth(6), .dataWidth(4)) rom_1 (.addr(Opcode), .data(rom_1_data));  // open: sel
  // Probe on rom_2_data
  ROM #(.addrWidth(6), .dataWidth(4)) rom_2 (.addr(Funct), .data(rom_2_data));  // open: sel
  Multiplexer #(.select(2), .width(4), .enable("false")) multiplexer_1 (
    .in0(4'b0000), .in1(4'b0001), .in2(rom_2_data), .in3(rom_1_data), .out(ALUOp), .sel(ALUClass));
  // Probe on ALUOp

  // Notes on the sheet:
  //   contents of rom_1 (hex, n*v repeats v):
  //   10*0 7 0 4 5 6
  //   contents of rom_2 (hex, n*v repeats v):
  //   8 0 9 a 20*0 2 0 3 7*0 1 0 4 5 6 0 0 0 7
endmodule
