// Logisim project procesor.circ as structural Verilog: 1 circuit, main circuit procesor
module procesor (
  input  Clock
);

  wire ALUSRC, BRANCH, BRANCHINV, BRANCHSIGNED, CLK, FLAGSEL, FUNCT_EQ_8, JR_FLAG, JR_NOT, JUMP, JUMP_CU,
       MEM2REG, MEMREAD, MEMWRITE, OPCODE_EQ_0, PC_SEL1, REGDST, REGWRITE, REGWRITE_CU, xor_1_out, ZERO;
  wire [3:0] ALUOP;
  wire [4:0] multiplexer_5_out;
  wire [5:0] FUNCT, Opcode_t;
  wire [15:6] IMM16;
  wire [31:0] ALU_B, ALU_RES, BR_TGT, JUMP_TGT, MEM_OUT, NPC, PC4, PC_NOBR, PC_OUT, RD1, RD2, SIGN_EXT,
       WB_DATA;
  wire [31:16] INSTR;

  // Probe on Opcode_t
  // Probe on JR_FLAG
  Adder #(.width(32)) adder_1 (.a(PC_OUT), .b(32'h1), .out(PC4));  // open: cin, cout
  // Probe on PC_OUT
  Register #(.width(32)) PC (.D(NPC), .Q(PC_OUT), .clk(CLK));  // open: en, clr
  // Probe on PC_OUT
  not not_1 (JR_NOT, JR_FLAG);
  or or_1 (JUMP, JUMP_CU, JR_FLAG);
  and and_1 (REGWRITE, REGWRITE_CU, JR_NOT);
  Multiplexer #(.enable("false")) multiplexer_1 (.in0(ZERO), .in1(ALU_RES[31]), .out(FLAGSEL), .sel(BRANCHSIGNED));
  Clock u_Clock (.out(CLK));
  Comparator #(.width(6)) comparator_1 (
    .a({INSTR[31:28], BRANCHSIGNED, BRANCHINV}), .b({6{1'b0}}), .eq(OPCODE_EQ_0));  // open: gt, lt
  Comparator #(.width(6)) comparator_2 (.a(FUNCT), .b(6'b001000), .eq(FUNCT_EQ_8));  // open: gt, lt
  // Probe on PC_OUT[7:0]
  // OR_Gate or_2 has open pins: in1=Clock, out=open
  // Probe on JUMP
  Multiplexer #(.width(32), .enable("false")) multiplexer_2 (
    .in0({{6{1'b0}}, INSTR[25:16], IMM16, FUNCT}), .in1(RD1), .out(JUMP_TGT), .sel(JR_FLAG));
  // Probe on {INSTR[31:28], BRANCHSIGNED, BRANCHINV, INSTR[25:16], IMM16, FUNCT}
  ROM #(.dataWidth(32)) rom_1 (
    .addr(PC_OUT[7:0]), .data({INSTR[31:28], BRANCHSIGNED, BRANCHINV, INSTR[25:16], IMM16, FUNCT}));  // open: sel
  and and_2 (JR_FLAG, OPCODE_EQ_0, FUNCT_EQ_8);
  Adder #(.width(32)) adder_2 (.a(PC4), .b(SIGN_EXT), .out(BR_TGT));  // open: cin, cout
  xor xor_1 (xor_1_out, FLAGSEL, BRANCHINV);
  // Probe on JR_FLAG
  and and_3 (PC_SEL1, BRANCH, xor_1_out);
  Multiplexer #(.width(32), .enable("false")) multiplexer_3 (.in0(PC4), .in1(BR_TGT), .out(PC_NOBR), .sel(PC_SEL1));
  assign SIGN_EXT = {{16{IMM16[15]}}, {IMM16, FUNCT}};  // Bit_Extender bit_extender_1
  // Probe on {INSTR[31:28], BRANCHSIGNED, BRANCHINV}
  // Probe on FUNCT
  // Probe on INSTR[25:21]
  // Probe on INSTR[20:16]
  Multiplexer #(.width(32), .enable("false")) multiplexer_4 (.in0(PC_NOBR), .in1(JUMP_TGT), .out(NPC), .sel(JUMP));
  // Probe on REGWRITE
  // Probe on NPC
  jednostka_sterujaca jednostka_sterujaca_1 (
    .Opcode({INSTR[31:28], BRANCHSIGNED, BRANCHINV}), .Funct(FUNCT), .RegDst(REGDST), .ALUSrc(ALUSRC),
    .MemtoReg(MEM2REG), .RegWrite(REGWRITE_CU), .MemRead(MEMREAD), .MemWrite(MEMWRITE), .Branch(BRANCH),
    .Jump(JUMP_CU), .ALUOp(ALUOP));  // open: ALUClass0, ControlWord, ALUClass1
  // Probe on RD2
  // Probe on ALUOP
  // Probe on multiplexer_5_out
  rejestry rejestry_1 (
    .RA1(INSTR[25:21]), .Clock(CLK), .RA2(INSTR[20:16]), .clear(1'b0), .WA(multiplexer_5_out),
    .RegWrite(REGWRITE), .Write_data(WB_DATA), .Read_data_1(RD1), .Read_data_2(RD2));
  // Probe on BRANCH
  Multiplexer #(.width(5)) multiplexer_5 (
    .in0(INSTR[20:16]), .in1(IMM16[15:11]), .out(multiplexer_5_out), .sel(REGDST));  // open: en
  // Probe on RD1
  // Probe on JUMP_CU
  // Probe on REGDST
  // Probe on ALUSRC
  // Probe on IMM16[15:11]
  // Probe on ALU_B
  Multiplexer #(.width(32), .enable("false")) multiplexer_6 (.in0(RD2), .in1(SIGN_EXT), .out(ALU_B), .sel(ALUSRC));
  alu_stage17_builtin_mux_core6_zero alu_stage17_builtin_mux_core6_zero_1 (
    .A(RD1), .B(ALU_B), .ALUOp(ALUOP), .shamt(IMM16[10:6]), .Negative(ALU_RES[31]), .Result(ALU_RES),
    .Zero(ZERO));
  // Probe on IMM16[10:6]
  // Probe on ALU_RES
  // Probe on ALU_RES
  RAM #(.dataWidth(32), .bus("separate")) ram_1 (
    .addr(ALU_RES[7:0]), .din(RD2), .data(MEM_OUT), .str(MEMWRITE), .clk(CLK), .ld(MEMREAD));  // open: sel, clr
  Multiplexer #(.width(32), .enable("false")) multiplexer_7 (
    .in0(ALU_RES), .in1(MEM_OUT), .out(WB_DATA), .sel(MEM2REG));

  // Other names for the same wires on the sheet: NEGATIVE = ALU_RES[31]; IMM16[5:0] = FUNCT;
  //   INSTR (some bits) = {BRANCHSIGNED, BRANCHINV, IMM16, FUNCT}; JUMP_TGT_CU[25:0] = {INSTR[25:16], IMM16, FUNCT};
  //   SHAMT_BUS[4:0] = IMM16[10:6]; RD[4:0] = IMM16[15:11]; RT[4:0] = INSTR[20:16]; RS[4:0] = INSTR[25:21];
  //   OPCODE[5:0] = {INSTR[31:28], BRANCHSIGNED, BRANCHINV}

  // Notes on the sheet:
  //   test AND instead of SUBTRACTOR
  //   Cycle beetwen Clock 0 -> 1 like 30 times
  //   [TODO] Replace PIN clock with actual clock
  //   Main file. Bauble sort pre-loaded
  //   ROM load - bauble_sort.hex
  //   Tick frequency -64Hz ?
  //   syf ale moze sie przydaxd
  //   RAM not loaded
  //   RAM lodad - ram_data.hex
endmodule
