// Logisim project rejestry.circ as structural Verilog: 1 circuit, main circuit rejestry
// Rejestry
module rejestry (
  input  Clock,
  input  [4:0] RA1,
  input  clear,
  input  [4:0] RA2,
  input  [31:0] Write_data,
  input  RegWrite,
  input  [4:0] WA,
  output [31:0] Read_data_2,
  output [31:0] Read_data_1
);

  wire enR1, enR2, enR3, enR4, enR5, enR6, enR7, enR8, enR9, enR10, enR11, enR12, enR13, enR14, enR15, enR16,
       enR17, enR18, enR19, enR20, enR21, enR22, enR23, enR24, enR25, enR26, enR27, enR28, enR29, enR30,
       enR31;
  wire [31:0] R0out, R1out, R2out, R3out, R4out, R5out, R6out, R7out, R8out, R9out, R10out, R11out, R12out,
       R13out, R14out, R15out, R16out, R17out, R18out, R19out, R20out, R21out, R22out, R23out, R24out,
       R25out, R26out, R27out, R28out, R29out, R30out, R31out;

  // Probe on Write_data
  Register #(.width(32)) register_1 (.D(Write_data), .en(1'b0), .Q(R0out), .clk(Clock), .clr(clear));
  // Probe on Write_data
  Register #(.width(32)) register_2 (.D(Write_data), .en(enR8), .Q(R8out), .clk(Clock), .clr(clear));
  // Probe on Write_data
  // Probe on Write_data
  Demultiplexer #(.select(5), .enable("false")) demultiplexer_1 (
    .out1(enR1), .out2(enR2), .out3(enR3), .out4(enR4), .out5(enR5), .out6(enR6), .out7(enR7), .out8(enR8),
    .out9(enR9), .out10(enR10), .out11(enR11), .out12(enR12), .out13(enR13), .out14(enR14), .out15(enR15),
    .out16(enR16), .out17(enR17), .out18(enR18), .out19(enR19), .out20(enR20), .out21(enR21), .out22(enR22),
    .out23(enR23), .out24(enR24), .out25(enR25), .out26(enR26), .out27(enR27), .out28(enR28), .out29(enR29),
    .out30(enR30), .out31(enR31), .in(RegWrite), .sel(WA));  // open: out0
  // Probe on R0out
  // Probe on R2out
  // Probe on R4out
  // Probe on R6out
  // Probe on R8out
  // Probe on R10out
  // Probe on R12out
  // Probe on R14out
  // Probe on R0out
  // Probe on R8out
  // Probe on R16out
  Register #(.width(32)) register_3 (.D(Write_data), .en(enR16), .Q(R16out), .clk(Clock), .clr(clear));
  // Probe on R24out
  Register #(.width(32)) register_4 (.D(Write_data), .en(enR24), .Q(R24out), .clk(Clock), .clr(clear));
  // Probe on R1out
  // Probe on R3out
  // Probe on R5out
  // Probe on R7out
  // Probe on R9out
  // Probe on R11out
  // Probe on R13out
  // Probe on R15out
  // Probe on Write_data
  // Probe on Write_data
  // Probe on Write_data
  // Probe on Write_data
  // Probe on R1out
  Register #(.width(32)) register_5 (.D(Write_data), .en(enR1), .Q(R1out), .clk(Clock), .clr(clear));
  // Probe on R9out
  Register #(.width(32)) register_6 (.D(Write_data), .en(enR9), .Q(R9out), .clk(Clock), .clr(clear));
  // Probe on R17out
  Register #(.width(32)) register_7 (.D(Write_data), .en(enR17), .Q(R17out), .clk(Clock), .clr(clear));
  // Probe on R25out
  Register #(.width(32)) register_8 (.D(Write_data), .en(enR25), .Q(R25out), .clk(Clock), .clr(clear));
  // Probe on Write_data
  // Probe on Write_data
  Multiplexer #(.select(5), .width(32), .enable("false")) multiplexer_1 (
    .in0(R0out), .in1(R1out), .in2(R2out), .in3(R3out), .in4(R4out), .in5(R5out), .in6(R6out), .in7(R7out),
    .in8(R8out), .in9(R9out), .in10(R10out), .in11(R11out), .in12(R12out), .in13(R13out), .in14(R14out),
    .in15(R15out), .in16(R16out), .in17(R17out), .in18(R18out), .in19(R19out), .in20(R20out), .in21(R21out),
    .in22(R22out), .in23(R23out), .in24(R24out), .in25(R25out), .in26(R26out), .in27(R27out), .in28(R28out),
    .in29(R29out), .in30(R30out), .in31(R31out), .out(Read_data_1), .sel(RA1));
  // Probe on R16out
  // Probe on R18out
  // Probe on R20out
  // Probe on R22out
  // Probe on R24out
  // Probe on R26out
  // Probe on R28out
  // Probe on R30out
  Register #(.width(32)) register_9 (.D(Write_data), .en(enR2), .Q(R2out), .clk(Clock), .clr(clear));
  Register #(.width(32)) register_10 (.D(Write_data), .en(enR10), .Q(R10out), .clk(Clock), .clr(clear));
  // Probe on Write_data
  Register #(.width(32)) register_11 (.D(Write_data), .en(enR18), .Q(R18out), .clk(Clock), .clr(clear));
  // Probe on Write_data
  Register #(.width(32)) register_12 (.D(Write_data), .en(enR26), .Q(R26out), .clk(Clock), .clr(clear));
  // Probe on R17out
  // Probe on R19out
  // Probe on R21out
  // Probe on R23out
  // Probe on R25out
  // Probe on R27out
  // Probe on R29out
  // Probe on R31out
  // Probe on R2out
  // Probe on R10out
  // Probe on R18out
  // Probe on R26out
  // Probe on Write_data
  // Probe on Write_data
  // Probe on Write_data
  // Probe on Write_data
  // Probe on R3out
  Register #(.width(32)) register_13 (.D(Write_data), .en(enR3), .Q(R3out), .clk(Clock), .clr(clear));
  // Probe on R11out
  Register #(.width(32)) register_14 (.D(Write_data), .en(enR11), .Q(R11out), .clk(Clock), .clr(clear));
  // Probe on R19out
  Register #(.width(32)) register_15 (.D(Write_data), .en(enR19), .Q(R19out), .clk(Clock), .clr(clear));
  // Probe on R27out
  Register #(.width(32)) register_16 (.D(Write_data), .en(enR27), .Q(R27out), .clk(Clock), .clr(clear));
  Multiplexer #(.select(5), .width(32), .enable("false")) multiplexer_2 (
    .in0(R0out), .in1(R1out), .in2(R2out), .in3(R3out), .in4(R4out), .in5(R5out), .in6(R6out), .in7(R7out),
    .in8(R8out), .in9(R9out), .in10(R10out), .in11(R11out), .in12(R12out), .in13(R13out), .in14(R14out),
    .in15(R15out), .in16(R16out), .in17(R17out), .in18(R18out), .in19(R19out), .in20(R20out), .in21(R21out),
    .in22(R22out), .in23(R23out), .in24(R24out), .in25(R25out), .in26(R26out), .in27(R27out), .in28(R28out),
    .in29(R29out), .in30(R30out), .in31(R31out), .out(Read_data_2), .sel(RA2));
  // Probe on Write_data
  // Probe on Write_data
  // Probe on Write_data
  // Probe on Write_data
  // Probe on R4out
  Register #(.width(32)) register_17 (.D(Write_data), .en(enR4), .Q(R4out), .clk(Clock), .clr(clear));
  // Probe on R12out
  Register #(.width(32)) register_18 (.D(Write_data), .en(enR12), .Q(R12out), .clk(Clock), .clr(clear));
  // Probe on R20out
  Register #(.width(32)) register_19 (.D(Write_data), .en(enR20), .Q(R20out), .clk(Clock), .clr(clear));
  // Probe on R28out
  Register #(.width(32)) register_20 (.D(Write_data), .en(enR28), .Q(R28out), .clk(Clock), .clr(clear));
  // Probe on Write_data
  // Probe on Write_data
  Register #(.width(32)) register_21 (.D(Write_data), .en(enR5), .Q(R5out), .clk(Clock), .clr(clear));
  Register #(.width(32)) register_22 (.D(Write_data), .en(enR13), .Q(R13out), .clk(Clock), .clr(clear));
  // Probe on Write_data
  Register #(.width(32)) register_23 (.D(Write_data), .en(enR21), .Q(R21out), .clk(Clock), .clr(clear));
  // Probe on Write_data
  Register #(.width(32)) register_24 (.D(Write_data), .en(enR29), .Q(R29out), .clk(Clock), .clr(clear));
  // Probe on R5out
  // Probe on R13out
  // Probe on R21out
  // Probe on R29out
  // Probe on Write_data
  // Probe on Write_data
  // Probe on Write_data
  // Probe on Write_data
  // Probe on R6out
  Register #(.width(32)) register_25 (.D(Write_data), .en(enR6), .Q(R6out), .clk(Clock), .clr(clear));
  // Probe on R14out
  Register #(.width(32)) register_26 (.D(Write_data), .en(enR14), .Q(R14out), .clk(Clock), .clr(clear));
  // Probe on R22out
  Register #(.width(32)) register_27 (.D(Write_data), .en(enR22), .Q(R22out), .clk(Clock), .clr(clear));
  // Probe on R30out
  Register #(.width(32)) register_28 (.D(Write_data), .en(enR30), .Q(R30out), .clk(Clock), .clr(clear));
  // Probe on Write_data
  // Probe on Write_data
  // Probe on Write_data
  // Probe on Write_data
  // Probe on R7out
  Register #(.width(32)) register_29 (.D(Write_data), .en(enR7), .Q(R7out), .clk(Clock), .clr(clear));
  // Probe on R15out
  Register #(.width(32)) register_30 (.D(Write_data), .en(enR15), .Q(R15out), .clk(Clock), .clr(clear));
  // Probe on R23out
  Register #(.width(32)) register_31 (.D(Write_data), .en(enR23), .Q(R23out), .clk(Clock), .clr(clear));
  // Probe on R31out
  Register #(.width(32)) register_32 (.D(Write_data), .en(enR31), .Q(R31out), .clk(Clock), .clr(clear));

  // Other names for the same wires on the sheet: clk = Clock; clr = clear; RA[31:0] = Read_data_1;
  //   RB[31:0] = Read_data_2; Rin[31:0] = Write_data
endmodule
