// Logisim project procesor_riscuva1_full.circ as structural Verilog: 1 circuit, main circuit main
module main (
  output [7:0] out_1,
  output [7:0] out_2,
  output [7:0] out_3,
  output [7:0] out_4,
  output [9:0] out_5,
  output [13:0] out_6,
  output [7:0] out_7,
  output [7:0] out_8,
  output [7:0] out_9,
  output out_10,
  output out_11,
  output out_12,
  output out_13
);

  wire aluCarry, anyBit, arithCarry, arithCinX, B1_Clk, B1_E1, B1_E2, B1_E3, B1_E4, B1_E5, B1_E6, E1, E2, E3,
       E4, E5, E6, flagEn, is_ALU, is_GOTO, is_JP, is_LOAD, is_MISC, jpTaken, logicCarry, M_E1, M_E2, M_E3,
       M_E4, M_E5, M_E6, nA0, nA1, nB1, nC, ncin, nRNhi, nZ, opB_eq01, opB_eq11, rawCout, shiftCarry,
       validFlag, we0, we1, zIsZero, zor01, zor23, zor45, zor67, zor0123, zor4567;
  wire [0:0] jsel;
  wire [7:0] altM, andOut, arithOut, b0_busM, b0_busN, b1_busM, b1_busN, B1_C1, B1_C2, B1_C3, B1_C4, B1_C5,
       B1_C6, B1_R1, B1_R2, B1_R3, B1_R4, B1_R5, B1_R6, C1, C2, C3, C4, C5, C6, dataBus, logicOut, M_C1,
       M_C2, M_C3, M_C4, M_C5, M_C6, M_R5, M_R6, notM, orOut, R1, R2, R3, R4, R5, R6, ramData, shiftOut,
       xnorOut, xorOut;
  wire [7:7] shrOut;
  wire [9:0] incPC, nextPC;

  Clock clock_1 (.out(B1_Clk));
  assign andOut = out_7 & out_8;  // AND_Gate and_1, 8 bits wide
  assign orOut = out_7 | out_8;  // OR_Gate or_1, 8 bits wide
  assign xorOut = out_7 ^ out_8;  // XOR_Gate xor_1, 8 bits wide
  assign notM = ~out_8;  // NOT_Gate not_1, 8 bits wide
  not not_2 (ncin, out_10);
  Multiplexer #(.select(2), .width(8)) multiplexer_1 (
    .in0(logicOut), .in1(arithOut), .in2(shiftOut), .in3(ramData), .out(out_9), .sel(out_6[11:10]), .en(1'b1));
  Multiplexer #(.select(2), .width(1)) multiplexer_2 (
    .in0(logicCarry), .in1(arithCarry), .in2(shiftCarry), .in3(logicCarry), .out(aluCarry),
    .sel(out_6[11:10]), .en(1'b1));
  not not_3 (nZ, out_11);
  not not_4 (nC, out_10);
  assign xnorOut = ~xorOut;  // NOT_Gate not_5, 8 bits wide
  Register u_R1 (.D(C1), .en(E1), .Q(R1), .clk(B1_Clk), .clr(1'b0));
  Register u_R3 (.D(C3), .en(E3), .Q(R3), .clk(B1_Clk), .clr(1'b0));
  Register u_R5 (.D(C5), .en(E5), .Q(R5), .clk(B1_Clk), .clr(1'b0));
  Multiplexer #(.select(3), .width(8), .enable("false")) multiplexer_3 (
    .in0(R1), .in1(R2), .in2(R3), .in3(R4), .in4(R5), .in5(R6), .out(b0_busN), .sel(out_6[2:0]));  // open: in6, in7
  Register R1_2 (.D(B1_C1), .en(B1_E1), .Q(B1_R1), .clk(B1_Clk), .clr(1'b0));
  Register R3_2 (.D(B1_C3), .en(B1_E3), .Q(B1_R3), .clk(B1_Clk), .clr(1'b0));
  Register R5_2 (.D(B1_C5), .en(B1_E5), .Q(B1_R5), .clk(B1_Clk), .clr(1'b0));
  Multiplexer #(.select(3), .width(8), .enable("false")) multiplexer_4 (
    .in0(B1_R1), .in1(B1_R2), .in2(B1_R3), .in3(B1_R4), .in4(B1_R5), .in5(B1_R6), .out(b1_busN),
    .sel(out_6[2:0]));  // open: in6, in7
  or or_2 (zor01, out_9[0], out_9[1]);
  or or_3 (zor23, out_9[2], out_9[3]);
  or or_4 (zor45, out_9[4], out_9[5]);
  or or_5 (zor67, out_9[6], out_9[7]);
  Multiplexer #(.select(2), .width(1)) multiplexer_5 (
    .in0(out_11), .in1(nZ), .in2(out_10), .in3(nC), .out(validFlag), .sel(out_6[11:10]), .en(1'b1));
  Multiplexer #(.select(2), .width(8)) multiplexer_6 (
    .in0(out_8), .in1(out_8), .in2(notM), .in3(notM), .out(altM), .sel(out_6[9:8]), .en(1'b1));
  Multiplexer #(.select(2), .width(1)) multiplexer_7 (
    .in0(1'b0), .in1(out_10), .in2(1'b1), .in3(ncin), .out(arithCinX), .sel(out_6[9:8]), .en(1'b1));
  Register u_R2 (.D(C2), .en(E2), .Q(R2), .clk(B1_Clk), .clr(1'b0));
  Register u_R4 (.D(C4), .en(E4), .Q(R4), .clk(B1_Clk), .clr(1'b0));
  Register u_R6 (.D(C6), .en(E6), .Q(R6), .clk(B1_Clk), .clr(1'b0));
  Multiplexer #(.select(3), .width(8), .enable("false")) multiplexer_8 (
    .in0(R1), .in1(R2), .in2(R3), .in3(R4), .in4(R5), .in5(R6), .out(b0_busM), .sel(out_6[6:4]));  // open: in6, in7
  Register R2_2 (.D(B1_C2), .en(B1_E2), .Q(B1_R2), .clk(B1_Clk), .clr(1'b0));
  Register R4_2 (.D(B1_C4), .en(B1_E4), .Q(B1_R4), .clk(B1_Clk), .clr(1'b0));
  Register R6_2 (.D(B1_C6), .en(B1_E6), .Q(B1_R6), .clk(B1_Clk), .clr(1'b0));
  Multiplexer #(.select(3), .width(8), .enable("false")) multiplexer_9 (
    .in0(B1_R1), .in1(B1_R2), .in2(B1_R3), .in3(B1_R4), .in4(B1_R5), .in5(B1_R6), .out(b1_busM),
    .sel(out_6[6:4]));  // open: in6, in7
  Multiplexer #(.select(2), .width(8)) multiplexer_10 (
    .in0(out_8), .in1(xnorOut), .in2(orOut), .in3(andOut), .out(logicOut), .sel(out_6[9:8]), .en(1'b1));
  Multiplexer #(.select(2), .width(1)) multiplexer_11 (
    .in0(out_10), .in1(out_10), .in2(1'b0), .in3(1'b1), .out(logicCarry), .sel(out_6[9:8]), .en(1'b1));
  Multiplexer #(.select(2), .width(1)) multiplexer_12 (
    .in0(out_7[7]), .in1(out_10), .in2(out_7[0]), .in3(1'b0), .out(shrOut[7]), .sel(out_6[9:8]), .en(1'b1));
  or or_6 (zor0123, zor01, zor23);
  or or_7 (zor4567, zor45, zor67);
  Adder #(.width(8)) adder_1 (.a(out_7), .b(altM), .out(arithOut), .cin(arithCinX), .cout(rawCout));
  or or_8 (anyBit, zor0123, zor4567);
  Demultiplexer #(.select(3), .width(8)) demultiplexer_1 (
    .out0(C1), .out1(C2), .out2(C3), .out3(C4), .out4(C5), .out5(C6), .in(dataBus), .sel(out_6[2:0]), .en(we0));  // open: out6, out7
  Demultiplexer #(.select(3)) demultiplexer_2 (
    .out0(E1), .out1(E2), .out2(E3), .out3(E4), .out4(E5), .out5(E6), .in(1'b1), .sel(out_6[2:0]), .en(we0));  // open: out6, out7
  Demultiplexer #(.select(3), .width(8)) demultiplexer_3 (
    .out0(B1_C1), .out1(B1_C2), .out2(B1_C3), .out3(B1_C4), .out4(B1_C5), .out5(B1_C6), .in(dataBus),
    .sel(out_6[2:0]), .en(we1));  // open: out6, out7
  Demultiplexer #(.select(3)) demultiplexer_4 (
    .out0(B1_E1), .out1(B1_E2), .out2(B1_E3), .out3(B1_E4), .out4(B1_E5), .out5(B1_E6), .in(1'b1),
    .sel(out_6[2:0]), .en(we1));  // open: out6, out7
  xor xor_2 (arithCarry, rawCout, out_6[9]);
  not not_6 (zIsZero, anyBit);
  Multiplexer #(.select(2), .width(8)) multiplexer_13 (
    .in0({shrOut[7], out_7[7:1]}), .in1({shrOut[7], out_7[7:1]}), .in2({shrOut[7], out_7[7:1]}),
    .in3({out_7[6:0], out_7[7]}), .out(shiftOut), .sel(out_6[9:8]), .en(1'b1));
  Multiplexer #(.select(2), .width(1)) multiplexer_14 (
    .in0(out_7[0]), .in1(out_7[0]), .in2(out_7[0]), .in3(out_7[7]), .out(shiftCarry), .sel(out_6[9:8]),
    .en(1'b1));
  not not_7 (nRNhi, out_6[3]);
  and and_2 (we0, out_12, nRNhi);
  and and_3 (we1, out_12, out_6[3]);
  Multiplexer #(.select(2), .width(8)) multiplexer_15 (
    .in0(b0_busN), .in1(b1_busN), .in2(b0_busN), .in3(b0_busN), .out(out_7), .sel({1'b0, out_6[3]}), .en(1'b1));
  Multiplexer #(.select(2), .width(8)) multiplexer_16 (
    .in0(b0_busM), .in1(b1_busM), .in2(b0_busM), .in3(b0_busM), .out(out_8), .sel({1'b0, out_6[7]}), .en(1'b1));
  not not_8 (nA1, out_6[13]);
  not not_9 (nA0, out_6[12]);
  not not_10 (nB1, out_6[11]);
  and and_4 (is_JP, nA1, out_6[12]);
  and and_5 (is_MISC, nA1, nA0);
  and and_6 (is_LOAD, out_6[13], nA0);
  and and_7 (is_ALU, out_6[13], out_6[12]);
  and and_8 (opB_eq01, nB1, out_6[10]);
  and and_9 (opB_eq11, out_6[11], out_6[10]);
  and and_10 (is_GOTO, is_MISC, opB_eq01);
  and and_11 (out_13, is_MISC, opB_eq11);
  or or_9 (out_12, is_LOAD, is_ALU);
  and and_12 (jpTaken, is_JP, validFlag);
  and and_13 (flagEn, is_ALU, opB_eq01);
  or or_10 (jsel[0], is_GOTO, jpTaken);
  Multiplexer #(.select(2), .width(8)) multiplexer_17 (
    .in0(out_9), .in1(out_6[11:4]), .in2(out_9), .in3(out_9), .out(dataBus), .sel({1'b0, is_LOAD}), .en(1'b1));
  Register R1_3 (.D(M_C1), .en(M_E1), .Q(out_1), .clk(B1_Clk), .clr(1'b0));
  Register R3_3 (.D(M_C3), .en(M_E3), .Q(out_3), .clk(B1_Clk), .clr(1'b0));
  Register R5_3 (.D(M_C5), .en(M_E5), .Q(M_R5), .clk(B1_Clk), .clr(1'b0));
  Multiplexer #(.select(3), .width(8), .enable("false")) multiplexer_18 (
    .in0(out_1), .in1(out_2), .in2(out_3), .in3(out_4), .in4(M_R5), .in5(M_R6), .sel(out_8[2:0]));  // open: in6, in7, out
  Register #(.width(1)) register_1 (.D(aluCarry), .en(flagEn), .Q(out_10), .clk(B1_Clk), .clr(1'b0));
  Register #(.width(1)) register_2 (.D(zIsZero), .en(flagEn), .Q(out_11), .clk(B1_Clk), .clr(1'b0));
  Register R2_3 (.D(M_C2), .en(M_E2), .Q(out_2), .clk(B1_Clk), .clr(1'b0));
  Register R4_3 (.D(M_C4), .en(M_E4), .Q(out_4), .clk(B1_Clk), .clr(1'b0));
  Register R6_3 (.D(M_C6), .en(M_E6), .Q(M_R6), .clk(B1_Clk), .clr(1'b0));
  Multiplexer #(.select(3), .width(8), .enable("false")) multiplexer_19 (
    .in0(out_1), .in1(out_2), .in2(out_3), .in3(out_4), .in4(M_R5), .in5(M_R6), .sel(out_8[2:0]));  // open: in6, in7, out
  Register #(.width(10)) register_3 (.D(nextPC), .en(1'b1), .Q(out_5), .clk(B1_Clk), .clr(1'b0));
  Demultiplexer #(.select(3), .width(8)) demultiplexer_5 (
    .out0(M_C1), .out1(M_C2), .out2(M_C3), .out3(M_C4), .out4(M_C5), .out5(M_C6), .in(out_7),
    .sel(out_8[2:0]), .en(out_13));  // open: out6, out7
  Demultiplexer #(.select(3)) demultiplexer_6 (
    .out0(M_E1), .out1(M_E2), .out2(M_E3), .out3(M_E4), .out4(M_E5), .out5(M_E6), .in(1'b1),
    .sel(out_8[2:0]), .en(out_13));  // open: out6, out7
  Adder #(.width(10)) adder_2 (.a(out_5), .b(10'h1), .out(incPC), .cin(1'b0));  // open: cout
  Multiplexer #(.select(2), .width(10)) multiplexer_20 (
    .in0(incPC), .in1(out_6[9:0]), .in2(incPC), .in3(incPC), .out(nextPC), .sel({1'b0, jsel[0]}), .en(1'b1));
  RAM #(.bus("separate"), .addrWidth(8), .dataWidth(8)) ram_1 (
    .addr(out_8), .din(out_7), .data(ramData), .str(out_13), .sel(1'b1), .clk(B1_Clk), .ld(1'b1), .clr(1'b0));
  ROM #(.addrWidth(10), .dataWidth(14)) rom_1 (.addr(out_5), .data(out_6));  // open: sel

  // Other names for the same wires on the sheet: aluOut[7:0] = out_9; zb0 = out_9[0]; zb1 = out_9[1]; zb2 = out_9[2];
  //   zb3 = out_9[3]; zb4 = out_9[4]; zb5 = out_9[5]; zb6 = out_9[6]; zb7 = out_9[7]; busM[7:0] = out_8;
  //   busM3[2:0] = out_8[2:0]; M_AddA[2:0] = out_8[2:0]; M_AddB[2:0] = out_8[2:0]; busMsel[0] = out_6[7];
  //   immAddr[9:0] = out_6[9:0]; immData[7:0] = out_6[11:4]; INSTR[13:0] = out_6; jumpTgt[9:0] = out_6[9:0];
  //   rM[3:0] = out_6[7:4]; rMhi = out_6[7]; busNsel[0] = out_6[3]; rN[3:0] = out_6[3:0]; rNhi = out_6[3];
  //   cin = out_10; flagC = out_10; flagZ = out_11; AddA[2:0] = out_6[2:0]; B1_AddA[2:0] = out_6[2:0];
  //   rN3[2:0] = out_6[2:0]; AddB[2:0] = out_6[6:4]; B1_AddB[2:0] = out_6[6:4]; rM3[2:0] = out_6[6:4];
  //   opC[1:0] = out_6[9:8]; opC1 = out_6[9]; opB[1:0] = out_6[11:10]; opB0 = out_6[10]; opB1 = out_6[11];
  //   opA[1:0] = out_6[13:12]; opA0 = out_6[12]; opA1 = out_6[13]; onJump = jsel[0]; Clk = B1_Clk; M_Clk = B1_Clk;
  //   M_R1[7:0] = out_1; M_R2[7:0] = out_2; M_R3[7:0] = out_3; M_R4[7:0] = out_4; PC[9:0] = out_5; portWrite = out_13;
  //   regWrite = out_12; busN[7:0] = out_7; n7 = out_7[7]; nHi7[6:0] = out_7[7:1];
  //   rolOut[7:0] = {out_7[6:0], out_7[7]}; shrOut[6:0] = out_7[7:1]; n0 = out_7[0]; nLo7[6:0] = out_7[6:0];
  //   shrTop = shrOut[7]; wbSel[0] = is_LOAD

  // Notes on the sheet:
  //   contents of rom_1 (hex, n*v repeats v):
  //   2003 3c34 2013 3c35 3042 3652 180b 2003 c35 2013 c34 2013 3c34 2023 3c35 3042 3652 1816 2013 c35
  //   2023 c34 2023 3c34 2033 3c35 3042 3652 1821 2023 c35 2033 c34 2003 3c34 2013 3c35 3042 3652 182c
  //   2003 c35 2013 c34 2013 3c34 2023 3c35 3042 3652 1837 2013 c35 2023 c34 2003 3c34 2013 3c35 3042 3652
  //   1842 2003 c35 2013 c34 442
endmodule
