// Logisim project procesor_riscuva1.circ as structural Verilog: 1 circuit, main circuit main
module main (
  output [7:0] out_1,
  output [13:0] out_2,
  output [7:0] out_3,
  output [7:0] out_4,
  output [7:0] out_5,
  output [7:0] out_6,
  output out_7,
  output out_8,
  output out_9,
  output out_10,
  output out_11,
  output out_12,
  output out_13
);

  wire Clk, E1, E2, E3, E4, E5, E6, flagCEn, is_MISC, jpTaken, M_E1, M_E2, M_E3, M_E4, M_E5, M_E6, nA0, nA1,
       nB1, opB_eq01, opB_eq11, subBorrow, undriven;
  wire [0:0] jsel;
  wire [7:0] aluOut, C1, C2, C3, C4, C5, C6, incPC, M_C1, M_C2, M_C3, M_C4, M_C5, M_C6, M_R1, M_R2, M_R3,
       M_R4, M_R5, M_R6, multiplexer_4_out, nextPC, R1, R2, R3, R4, R5, R6, subR;

  Clock clock_1 (.out(Clk));
  and and_1 (jpTaken, out_13, out_9);
  // Probe on R1
  Register u_R1 (.D(C1), .en(E1), .Q(R1), .clk(Clk), .clr(1'b0));
  Register u_R3 (.D(C3), .en(E3), .Q(R3), .clk(Clk), .clr(1'b0));
  Register u_R5 (.D(C5), .en(E5), .Q(R5), .clk(Clk), .clr(1'b0));
  Multiplexer #(.select(3), .width(8), .enable("false")) multiplexer_1 (
    .in0(R1), .in1(R2), .in2(R3), .in3(R4), .in4(R5), .in5(R6), .out(out_3), .sel(out_2[2:0]));  // open: in6, in7
  or or_1 (jsel[0], out_12, jpTaken);
  Register register_1 (.D(nextPC), .en(1'b1), .Q(out_1), .clk(Clk), .clr(1'b0));
  Register R1_2 (.D(M_C1), .en(M_E1), .Q(M_R1), .clk(Clk), .clr(1'b0));
  Register R3_2 (.D(M_C3), .en(M_E3), .Q(M_R3), .clk(Clk), .clr(1'b0));
  Register R5_2 (.D(M_C5), .en(M_E5), .Q(M_R5), .clk(Clk), .clr(1'b0));
  Multiplexer #(.select(3), .width(8), .enable("false")) multiplexer_2 (
    .in0(M_R1), .in1(M_R2), .in2(M_R3), .in3(M_R4), .in4(M_R5), .in5(M_R6), .out(out_6), .sel(out_4[2:0]));  // open: in6, in7
  // Probe on R2
  Register u_R2 (.D(C2), .en(E2), .Q(R2), .clk(Clk), .clr(1'b0));
  Register u_R4 (.D(C4), .en(E4), .Q(R4), .clk(Clk), .clr(1'b0));
  Register u_R6 (.D(C6), .en(E6), .Q(R6), .clk(Clk), .clr(1'b0));
  Multiplexer #(.select(3), .width(8), .enable("false")) multiplexer_3 (
    .in0(R1), .in1(R2), .in2(R3), .in3(R4), .in4(R5), .in5(R6), .out(out_4), .sel(out_2[6:4]));  // open: in6, in7
  Register R2_2 (.D(M_C2), .en(M_E2), .Q(M_R2), .clk(Clk), .clr(1'b0));
  Register R4_2 (.D(M_C4), .en(M_E4), .Q(M_R4), .clk(Clk), .clr(1'b0));
  Register R6_2 (.D(M_C6), .en(M_E6), .Q(M_R6), .clk(Clk), .clr(1'b0));
  Multiplexer #(.select(3), .width(8), .enable("false")) multiplexer_4 (
    .in0(M_R1), .in1(M_R2), .in2(M_R3), .in3(M_R4), .in4(M_R5), .in5(M_R6), .out(multiplexer_4_out),
    .sel(out_4[2:0]));  // open: in6, in7
  Adder adder_1 (.a(out_1), .b(8'h1), .out(incPC), .cin(1'b0));  // open: cout
  Multiplexer #(.select(2), .width(8)) multiplexer_5 (
    .in0(incPC), .in1(out_2[7:0]), .in2(incPC), .in3(incPC), .out(nextPC), .sel({1'b0, jsel[0]}), .en(1'b1));
  Demultiplexer #(.select(3), .width(8)) demultiplexer_1 (
    .out0(C1), .out1(C2), .out2(C3), .out3(C4), .out4(C5), .out5(C6), .in(out_5), .sel(out_2[2:0]), .en(out_7));  // open: out6, out7
  Demultiplexer #(.select(3)) demultiplexer_2 (
    .out0(E1), .out1(E2), .out2(E3), .out3(E4), .out4(E5), .out5(E6), .in(1'b1), .sel(out_2[2:0]), .en(out_7));  // open: out6, out7
  Demultiplexer #(.select(3), .width(8)) demultiplexer_3 (
    .out0(M_C1), .out1(M_C2), .out2(M_C3), .out3(M_C4), .out4(M_C5), .out5(M_C6), .in(out_3),
    .sel(out_4[2:0]), .en(out_8));  // open: out6, out7
  Demultiplexer #(.select(3)) demultiplexer_4 (
    .out0(M_E1), .out1(M_E2), .out2(M_E3), .out3(M_E4), .out4(M_E5), .out5(M_E6), .in(1'b1),
    .sel(out_4[2:0]), .en(out_8));  // open: out6, out7
  // Probe on undriven
  Subtractor subtractor_1 (.a(out_3), .b(out_4), .out(subR), .bin(1'b0), .bout(subBorrow));
  and and_2 (flagCEn, out_11, opB_eq01);
  Register #(.width(1)) register_2 (.D(subBorrow), .en(flagCEn), .Q(out_9), .clk(Clk), .clr(1'b0));
  not not_1 (nA1, out_2[13]);
  not not_2 (nA0, out_2[12]);
  not not_3 (nB1, out_2[11]);
  Multiplexer #(.select(2), .width(8)) multiplexer_6 (
    .in0(out_4), .in1(subR), .in2(out_4), .in3(out_6), .out(aluOut), .sel(out_2[11:10]), .en(1'b1));
  and and_3 (out_13, nA1, out_2[12]);
  and and_4 (is_MISC, nA1, nA0);
  and and_5 (out_10, out_2[13], nA0);
  and and_6 (out_11, out_2[13], out_2[12]);
  and and_7 (opB_eq01, nB1, out_2[10]);
  and and_8 (opB_eq11, out_2[11], out_2[10]);
  and and_9 (out_12, is_MISC, opB_eq01);
  and and_10 (out_8, is_MISC, opB_eq11);
  or or_2 (out_7, out_10, out_11);
  // Probe on out_7
  Multiplexer #(.select(2), .width(8)) multiplexer_7 (
    .in0(aluOut), .in1(out_2[11:4]), .in2(aluOut), .in3(aluOut), .out(out_5), .sel({1'b0, out_10}), .en(1'b1));
  ROM #(.dataWidth(14)) rom_1 (.addr(out_1), .data(out_2));  // open: sel
  // Probe on M_R1
  // Probe on M_R2
  // Probe on M_R3
  // Probe on M_R4

  // Other names for the same wires on the sheet: busM[7:0] = out_4; busM3[2:0] = out_4[2:0]; M_AddA[2:0] = out_4[2:0];
  //   M_AddB[2:0] = out_4[2:0]; busN[7:0] = out_3; dataBus[7:0] = out_5; flagC = out_9; AddA[2:0] = out_2[2:0];
  //   immAddr[7:0] = out_2[7:0]; INSTR[13:0] = out_2; rN[3:0] = out_2[3:0]; rN3[2:0] = out_2[2:0];
  //   AddB[2:0] = out_2[6:4]; immData[7:0] = out_2[11:4]; rM[3:0] = out_2[7:4]; rM3[2:0] = out_2[6:4];
  //   opC[1:0] = out_2[9:8]; opB[1:0] = out_2[11:10]; opB0 = out_2[10]; opB1 = out_2[11]; opA[1:0] = out_2[13:12];
  //   opA0 = out_2[12]; opA1 = out_2[13]; is_ALU = out_11; is_GOTO = out_12; is_JP = out_13; onJump = jsel[0];
  //   M_Clk = Clk; PC[7:0] = out_1; portWrite = out_8; ramData[7:0] = out_6; regWrite = out_7; is_LOAD = out_10;
  //   wbSel[0] = out_10

  // Notes on the sheet:
  //   contents of rom_1 (hex, n*v repeats v):
  //   20a4 2003 c34 2024 2013 c34 2034 2023 c34 20e4 2033 c34 2003 3c34 2013 3c35 3042 3652 1817 2003 c35
  //   2013 c34 2013 3c34 2023 3c35 3042 3652 1822 2013 c35 2023 c34 2023 3c34 2033 3c35 3042 3652 182d
  //   2023 c35 2033 c34 2003 3c34 2013 3c35 3042 3652 1838 2003 c35 2013 c34 2013 3c34 2023 3c35 3042 3652
  //   1843 2013 c35 2023 c34 2003 3c34 2013 3c35 3042 3652 184e 2003 c35 2013 c34 44e
endmodule
